// Logisim project Cache.circ as structural Verilog: 10 circuits, main circuit main
module main (
  input  EnableTestHalting,
  output [9:0] CorrectCounter,
  output [9:0] HitCounter,
  output [9:0] MissCounter,
  output [9:0] TestNumber,
  output [7:0] ByteRead,
  output [7:0] CorrectByteRead,
  output Halt
);

  wire and_3_out, and_4_out, and_5_out, CLK, CmdIsRead, Correct, CpuRead, CpuWrite, DidContain, HaltTesting,
       MaxItersReached, MemRead, MemWrite, not_1_out, not_2_out, not_4_out, NotDoneTesting, Ok2Count,
       or_1_out, Ready;
  wire [7:0] CpuWriteValue, MemAddress;
  wire [9:0] CpuAddress;
  wire [31:0] Line2Mem, LineFromMem;

  not not_1 (not_1_out, Ready);
  Clock clock_1 (.out(CLK));
  or or_1 (or_1_out, MaxItersReached, Ready);
  Counter #(.width(4), .max('h9)) MaxClocks (
    .load(Ready), .D(4'b0001), .count(not_1_out), .carry(MaxItersReached), .clk(CLK));  // open: Q, clr
  and and_1 (HaltTesting, EnableTestHalting, CmdIsRead, not_2_out);
  not not_2 (not_2_out, Correct);
  not not_3 (NotDoneTesting, Halt);
  Inputs inputs_1 (
    .HaltTesting(HaltTesting), .Ready(or_1_out), .CLK(CLK), .Done(Halt), .Read(CpuRead), .Write(CpuWrite),
    .Address(CpuAddress), .Value(CpuWriteValue), .TestNumber(TestNumber));
  Cache cache_1 (
    .CpuAddress(CpuAddress), .CpuRead(CpuRead), .CpuWrite(CpuWrite), .CpuWriteValue(CpuWriteValue),
    .CLK(CLK), .Ready(Ready), .DidContain(DidContain), .ByteRead(ByteRead), .MemAddress(MemAddress),
    .MemRead(MemRead), .MemWrite(MemWrite), .LineFromMem(LineFromMem), .Line2Mem(Line2Mem));
  // Probe on CpuRead
  // Probe on CpuWrite
  // Probe on CpuAddress
  // Probe on CpuWriteValue
  // Probe on TestNumber
  // Probe on CorrectByteRead
  // Probe on Correct
  // Probe on Ready
  // Probe on DidContain
  // Probe on ByteRead
  // Probe on MemAddress
  // Probe on MemRead
  // Probe on MemWrite
  // Probe on HitCounter
  // Probe on LineFromMem
  // Probe on Line2Mem
  not not_4 (not_4_out, HaltTesting);
  RAM #(.dataWidth(32), .bus("separate")) ram_1 (
    .addr(MemAddress), .din(Line2Mem), .data(LineFromMem), .str(MemWrite), .clk(CLK), .ld(MemRead));  // open: sel, clr
  and and_2 (Ok2Count, Ready, not_4_out, NotDoneTesting);
  and and_3 (and_3_out, Correct, Ok2Count);
  and and_4 (and_4_out, DidContain, Ok2Count);
  and and_5 (and_5_out, MemRead, NotDoneTesting);
  Checker checker_1 (
    .TestNumber(TestNumber), .YourByteRead(ByteRead), .CmdIsRead(CmdIsRead),
    .CorrectByteRead(CorrectByteRead), .Correct(Correct));
  Counter #(.width(10), .max('h3ff)) u_CorrectCounter (
    .count(and_3_out), .Q(CorrectCounter), .clk(CLK));  // open: load, D, carry, clr
  Counter #(.width(10), .max('h3ff)) u_HitCounter (
    .count(and_4_out), .Q(HitCounter), .clk(CLK));  // open: load, D, carry, clr
  Counter #(.width(10), .max('h3ff)) u_MissCounter (
    .count(and_5_out), .Q(MissCounter), .clk(CLK));  // open: load, D, carry, clr
  // Probe on CorrectCounter
  // Probe on HitCounter
  // Probe on MissCounter

  // Other names for the same wires on the sheet: DoneTesting = Halt

  // Notes on the sheet:
  //   Your Answer Inside Here
  //   Sayed Yoseph Sadat 914290757
  //   Muhammed Halbutogullari (913938544) 
endmodule

module Cache (
  input  [9:0] CpuAddress,
  input  CpuRead,
  input  CpuWrite,
  input  [7:0] CpuWriteValue,
  input  CLK,
  input  [31:0] LineFromMem,
  output Ready,
  output DidContain,
  output [7:0] ByteRead,
  output [7:0] MemAddress,
  output MemRead,
  output MemWrite,
  output [31:0] Line2Mem
);

  wire or_1_out, SavedRead, SavedWrite, Set, Set0_didcontain, Set0_memread, Set0_memwrite, Set1_didcontain,
       Set1_memread, Set1_memwrite, Start;
  wire [1:0] Offset;
  wire [2:0] currState, fsm_1_s02;
  wire [6:0] StoredTag, Tag;
  wire [7:0] SavedWriteValue, Set0_byteread, Set1_byteread;
  wire [31:0] Set0_line2mem, Set1_line2mem;

  or or_1 (or_1_out, CpuRead, CpuWrite);
  Register #(.width(10)) register_1 (.D(CpuAddress), .en(Start), .Q({Tag, Set, Offset}), .clk(CLK));  // open: clr
  Register #(.width(1)) register_2 (.D(CpuRead), .en(Start), .Q(SavedRead), .clk(CLK));  // open: clr
  Register #(.width(1)) register_3 (.D(CpuWrite), .en(Start), .Q(SavedWrite), .clk(CLK));  // open: clr
  Register register_4 (.D(CpuWriteValue), .en(Start), .Q(SavedWriteValue), .clk(CLK));  // open: clr
  and and_1 (Start, Ready, or_1_out);
  FSM fsm_1 (
    .S0(currState[0]), .S1(currState[1]), .S2(currState[2]), .Contains(DidContain), .Read(CpuRead),
    .Write(CpuWrite), .S02(fsm_1_s02[0]), .S12(fsm_1_s02[1]), .S22(fsm_1_s02[2]), .Ready(Ready));
  Register #(.width(3)) FSM_2 (.D(fsm_1_s02), .Q(currState), .clk(CLK));  // open: en, clr
  Set Set0 (
    .State(currState), .Set(Set), .Tag(Tag), .Offset(Offset), .CPURead(CpuRead), .CPUWrite(CpuWrite),
    .CpuWriteValue(CpuWriteValue), .LineFromMem(LineFromMem), .CLK(CLK), .This_Set(1'b0),
    .DidContain(Set0_didcontain), .ByteRead(Set0_byteread), .MemRead(Set0_memread), .MemWrite(Set0_memwrite),
    .Line2Mem(Set0_line2mem));
  Set Set1 (
    .State(currState), .Set(Set), .Tag(Tag), .Offset(Offset), .CPURead(CpuRead), .CPUWrite(CpuWrite),
    .CpuWriteValue(CpuWriteValue), .LineFromMem(LineFromMem), .CLK(CLK), .This_Set(1'b1),
    .DidContain(Set1_didcontain), .ByteRead(Set1_byteread), .MemRead(Set1_memread), .MemWrite(Set1_memwrite),
    .Line2Mem(Set1_line2mem));
  Multiplexer #(.enable("false")) multiplexer_1 (
    .in0(Set0_didcontain), .in1(Set1_didcontain), .out(DidContain), .sel(Set));
  Multiplexer #(.width(8), .enable("false")) multiplexer_2 (
    .in0(Set0_byteread), .in1(Set1_byteread), .out(ByteRead), .sel(Set));
  Multiplexer #(.enable("false")) multiplexer_3 (.in0(Set0_memread), .in1(Set1_memread), .out(MemRead), .sel(Set));
  Multiplexer #(.enable("false")) multiplexer_4 (.in0(Set0_memwrite), .in1(Set1_memwrite), .out(MemWrite), .sel(Set));
  Multiplexer #(.width(32), .enable("false")) multiplexer_5 (
    .in0(Set0_line2mem), .in1(Set1_line2mem), .out(Line2Mem), .sel(Set));
  Multiplexer #(.width(8), .enable("false")) multiplexer_6 (
    .in0({Tag, Set}), .in1({StoredTag, Set}), .out(MemAddress), .sel(MemWrite));

  // Notes on the sheet:
  //   Address Bits = 10
  //   Line Size = 4
  //   W = 3
  //   Num Sets = 2
  //   C =4*3*2 = 24bytes
  //   Tag bits = 7
  //   finite state machine
  //   Choosing which outputs to select from the two possible sets
endmodule

module Inputs (
  input  HaltTesting,
  input  Ready,
  input  CLK,
  output Done,
  output Read,
  output Write,
  output [9:0] Address,
  output [7:0] Value,
  output [9:0] TestNumber
);

  wire and_1_out, not_1_out, not_2_out;

  not not_1 (not_1_out, HaltTesting);
  not not_2 (not_2_out, Done);
  Counter #(.width(10), .max('h3ff), .ongoal("stay")) u_TestNumber (
    .count(and_1_out), .Q(TestNumber), .clk(CLK));  // open: load, D, carry, clr
  and and_1 (and_1_out, not_1_out, Ready, not_2_out);
  ROM #(.addrWidth(10), .dataWidth(21)) rom_1 (
    .addr(TestNumber), .data({Done, Read, Write, Address, Value}));  // open: sel

  // Notes on the sheet:
  //   contents of rom_1 (hex, n*v repeats v):
  //   80882 83fe6 4306b 83e0e 43701 42275 8280f 80304 41bd8 84371 43f77 41d70 4250b 44733 8253d 440d8
  //   82691 440c9 83d7c 43558 446bf 83837 842c9 43e0f 4059d 41556 80166 833b0 43a89 83142 8361c 42e66
  //   43eb6 42c00 43a0e 8165c 84682 8092a 83907 41f89 817b0 40855 82056 425e8 43ff2 8039f 42bd7 82137
  //   4416b 40273 8324a 814e4 44570 41c0f 429da 82640 8069c 8099e 414d5 41004 81beb 84113 419b1 81add
  //   83f35 425ff 829cd 40250 82945 4366d 40cc2 444f8 80814 81156 8446d 42a82 42bae 82578 41135 405d0
  //   8304b 82b3a 40972 822ba 4443a 42337 82506 80bd3 80560 83552 83955 81434 43096 43da1 81aa2 80305
  //   428e6 428cc 808a2 40e80 845f0 4215d 82765 82e29 40be5 82b74 42715 417a2 41fab 8452f 81c0a 83325
  //   44624 80205 42dfc 41333 40958 81348 42736 41069 84510 44669 826dd 8067e 408e4 44680 444e8 832ad
  //   821f8 83509 82d46 81184 432cd 80b77 4005a 440e0 81ea0 43d73 42b8c 80624 41468 42699 415ed 80fc1 0
  //   100000
endmodule

module Checker (
  input  [9:0] TestNumber,
  input  [7:0] YourByteRead,
  output CmdIsRead,
  output [7:0] CorrectByteRead,
  output Correct
);

  wire comparator_1_eq;
  wire [9:0] subtractor_1_out;

  // Probe on TestNumber
  Subtractor #(.width(10)) subtractor_1 (.a(TestNumber), .b(10'h1), .out(subtractor_1_out));  // open: bin, bout
  ROM #(.addrWidth(10), .dataWidth(9)) rom_1 (
    .addr(subtractor_1_out), .data({CmdIsRead, CorrectByteRead}));  // open: sel
  Comparator #(.mode("unsigned")) comparator_1 (
    .a(YourByteRead), .b(CorrectByteRead), .eq(comparator_1_eq));  // open: gt, lt
  and and_1 (Correct, comparator_1_eq, CmdIsRead);

  // Other names for the same wires on the sheet: Test_Number[9:0] = TestNumber

  // Notes on the sheet:
  //   Read Solutions
  //   contents of rom_1 (hex, n*v repeats v):
  //   1a3 1dc 6b 125 1 75 1dc 1c3 d8 1ab 77 70 b 33 10b d8 1c3 c9 174 58 bf 153 199 f 9d 56 1bb 13b 89 16c
  //   180 66 b6 0 e 107 1bf 1d8 167 89 118 55 1a2 e8 f2 1c3 d7 142 6b 73 1ab 18c 70 f da 1c3 14c 1d8 d5 4
  //   1d8 16b b1 1f4 1f2 ff 1da 50 1da 6d c2 f8 155 1c6 1f8 82 ae 1ff 35 d0 16b 1ae 72 175 3a 37 1ff 173
  //   1d0 158 167 1d5 96 a1 1f4 1c3 e6 cc 155 80 170 5d 1e6 166 e5 1ae 15 a2 ab 170 10f 13b 24 150 fc 33
  //   58 133 36 69 170 69 1c3 14c e4 80 e8 1ab 15d 158 1fc 135 cd 1e5 5a e0 104 73 8c 14c 68 99 ed 1a6
endmodule

module Evicted_Line (
  input  _0Valid,
  input  _1Valid,
  input  _2Valid,
  input  [1:0] Age_0,
  input  [1:0] Age_1,
  input  [1:0] Age_2,
  output [1:0] ChosenLine
);

  wire _0_1, _0_2, _1_0, _1_2, _2_0, _2_1, oldest1, oldest2;
  wire [1:0] multiplexer_1_out, oldestAmong0and1, oldestAmong0and2, oldestAmong1and2, oldestLine;

  Comparator #(.width(2), .mode("unsigned")) comparator_1 (.a(Age_0), .b(Age_1), .gt(_0_1), .lt(_1_0));  // open: eq
  Comparator #(.width(2), .mode("unsigned")) comparator_2 (.a(Age_1), .b(Age_2), .gt(_1_2), .lt(_2_1));  // open: eq
  Comparator #(.width(2), .mode("unsigned")) comparator_3 (.a(Age_0), .b(Age_2), .gt(_0_2), .lt(_2_0));  // open: eq
  and and_1 (oldest1, _1_2, _1_0);
  and and_2 (oldest2, _2_1, _2_0);
  Multiplexer #(.width(2), .enable("false")) multiplexer_1 (
    .in0(2'b00), .in1(2'b01), .out(multiplexer_1_out), .sel(oldest1));
  Multiplexer #(.width(2), .enable("false")) multiplexer_2 (
    .in0(2'b10), .in1(2'b01), .out(oldestAmong1and2), .sel(_1_2));
  Multiplexer #(.width(2), .enable("false")) multiplexer_3 (
    .in0(2'b10), .in1(2'b00), .out(oldestAmong0and2), .sel(_0_2));
  Multiplexer #(.width(2), .enable("false")) multiplexer_4 (
    .in0(2'b01), .in1(2'b00), .out(oldestAmong0and1), .sel(_0_1));
  Multiplexer #(.width(2), .enable("false")) multiplexer_5 (
    .in0(multiplexer_1_out), .in1(2'b10), .out(oldestLine), .sel(oldest2));
  Multiplexer #(.select(3), .width(2), .enable("false")) multiplexer_6 (
    .in0(oldestLine), .in1(oldestAmong1and2), .in2(oldestAmong0and2), .in3(2'b00), .in4(oldestAmong0and1),
    .in5(2'b01), .in6(2'b10), .in7(oldestLine), .out(ChosenLine), .sel({_2Valid, _1Valid, _0Valid}));

  // Notes on the sheet:
  //   Check if 0 is greater than 1. If so then we choose 0>1. If 0 is less than 1, then we choose 1 > 0. 
  //   Check if 1 is greater than 2. If so then we choose 1>2. If 0 1 is less than 2, then we choose 2 > 1. 
  //   Check if 0 is greater than 2. If so then we choose 0>2. If 0 is less than 2, then we choose 2 > 0. 
  //   If 1 is greater than 2 and 0, then 1 is the oldest.
  //   If 2 is greater than 1 and 0, then 2 is the oldest.
  //   Choosing a line to evict, based on which are valid
  //   Selecting the oldest line among all
  //   Selecting the oldest line among 1 and 2
  //   Selecting the oldest line among 0 and 2
  //   Selecting the oldest line among 0 and 1
endmodule

module IncrementAge (
  input  [1:0] ageOfEvicted,
  input  [1:0] currentAge,
  output [1:0] updatedAge
);

  wire comparator_1_eq;
  wire [1:0] adder_1_out;

  Comparator #(.width(2), .mode("unsigned")) comparator_1 (
    .a(ageOfEvicted), .b(currentAge), .eq(comparator_1_eq));  // open: gt, lt
  Adder #(.width(2)) adder_1 (.a(currentAge), .b(2'b01), .out(adder_1_out));  // open: cin, cout
  Multiplexer #(.width(2), .enable("false")) multiplexer_1 (
    .in0(adder_1_out), .in1(2'b00), .out(updatedAge), .sel(comparator_1_eq));
endmodule

module chooseBlock (
  input  Contains0,
  input  Contains1,
  input  Contains2,
  input  SetAge,
  output [1:0] Selected_Block
);

  wire and_1_out, or_1_out;
  wire [1:0] multiplexer_1_out, multiplexer_2_out;

  or or_1 (or_1_out, Contains0, Contains1, Contains2);
  Multiplexer #(.width(2), .enable("false")) multiplexer_1 (
    .in0(2'b00), .in1(2'b01), .out(multiplexer_1_out), .sel(Contains1));
  Multiplexer #(.width(2), .enable("false")) multiplexer_2 (
    .in0(multiplexer_1_out), .in1(2'b10), .out(multiplexer_2_out), .sel(Contains2));
  and and_1 (and_1_out, or_1_out, SetAge);
  Multiplexer #(.width(2), .enable("false")) multiplexer_3 (
    .in0(2'b11), .in1(multiplexer_2_out), .out(Selected_Block), .sel(and_1_out));

  // Notes on the sheet:
  //   Choosing the number of the block that contains the line
  //   If no block contains, or we are not setting the age, we select the 4th block which is nonexistent
endmodule

module Set (
  input  [2:0] State,
  input  Set,
  input  [6:0] Tag,
  input  [1:0] Offset,
  input  CPURead,
  input  CPUWrite,
  input  [7:0] CpuWriteValue,
  input  [31:0] LineFromMem,
  input  CLK,
  input  This_Set,
  output DidContain,
  output [7:0] ByteRead,
  output MemRead,
  output MemWrite,
  output [31:0] Line2Mem
);

  wire _0Contains, _0Dirty, _0Valid, _1Contains, _1Dirty, _1Valid, _2Contains, _2Dirty, _2Valid, and_1_out,
       Contains, Intialize, or_1_out, or_2_out, or_3_out, Ready, savedContains, SetAge, SetByte, setEnable,
       SetLine;
  wire [1:0] _0Age, _1Age, _2Age, ChosenBlock, evicted_line_1_chosenline, EvictedBlock, multiplexer_1_out,
       selectedblock;
  wire [7:0] _0Byte, _1Byte, _2Byte;
  wire [31:0] _0Line, _1Line, _2Line;

  Demultiplexer #(.select(3), .enable("false")) demultiplexer_1 (
    .out0(Intialize), .out1(Ready), .out2(MemWrite), .out3(MemRead), .out4(SetAge), .out5(SetLine),
    .out6(SetByte), .out7(Contains), .in(1'b1), .sel(State));
  or or_1 (or_1_out, _0Contains, _1Contains, _2Contains);
  Register #(.width(1)) u_State (.D(or_1_out), .en(Ready), .Q(savedContains), .clk(CLK));  // open: clr
  Multiplexer #(.width(2), .enable("false")) multiplexer_1 (
    .in0(ChosenBlock), .in1(EvictedBlock), .out(multiplexer_1_out), .sel(MemWrite));
  or or_2 (or_2_out, MemWrite, and_1_out);
  and and_1 (and_1_out, SetAge, savedContains);
  Comparator #(.width(1), .mode("unsigned")) comparator_1 (.a(Set), .b(This_Set), .eq(setEnable));  // open: gt, lt
  Register #(.width(2)) State_2 (.D(multiplexer_1_out), .en(or_2_out), .Q(selectedblock), .clk(CLK));  // open: clr
  Block Block0 (
    .State(State), .CPURead(CPURead), .CPUWrite(CPUWrite), .Tag(Tag), .Offset(Offset),
    .WriteValue(CpuWriteValue), .LineFromMem(LineFromMem), .SetEnable(setEnable), .CLK(CLK),
    .BlockNumber(2'b00), .Contains(_0Contains), .Valid(_0Valid), .Dirty(_0Dirty), .updatedAge(_0Age),
    .ByteRead(_0Byte), .Line2Mem(_0Line));
  Block Block1 (
    .State(State), .CPURead(CPURead), .CPUWrite(CPUWrite), .Tag(Tag), .Offset(Offset),
    .WriteValue(CpuWriteValue), .LineFromMem(LineFromMem), .SetEnable(setEnable), .CLK(CLK),
    .BlockNumber(2'b01), .Contains(_1Contains), .Valid(_1Valid), .Dirty(_1Dirty), .updatedAge(_1Age),
    .ByteRead(_1Byte), .Line2Mem(_1Line));
  Block Block2 (
    .State(State), .CPURead(CPURead), .CPUWrite(CPUWrite), .Tag(Tag), .Offset(Offset),
    .WriteValue(CpuWriteValue), .LineFromMem(LineFromMem), .SetEnable(setEnable), .CLK(CLK),
    .BlockNumber(2'b10), .Contains(_2Contains), .Valid(_2Valid), .Dirty(_2Dirty), .updatedAge(_2Age),
    .ByteRead(_2Byte), .Line2Mem(_2Line));
  Evicted_Line evicted_line_1 (
    ._0Valid(_0Valid), ._1Valid(_1Valid), ._2Valid(_2Valid), .Age_0(_0Age), .Age_1(_1Age), .Age_2(_2Age),
    .ChosenLine(evicted_line_1_chosenline));
  Multiplexer #(.width(2), .enable("false")) multiplexer_2 (
    .in0(2'b00), .in1(evicted_line_1_chosenline), .out(EvictedBlock), .sel(MemWrite));
  chooseBlock ChooseBlock (
    .Contains0(_0Contains), .Contains1(_1Contains), .Contains2(_2Contains), .SetAge(SetAge),
    .Selected_Block(ChosenBlock));
  or or_3 (or_3_out, _0Contains, _1Contains, _2Contains);
  not not_1 (DidContain, or_3_out);
  Multiplexer #(.select(2), .width(8), .enable("false")) multiplexer_3 (
    .in0(_0Byte), .in1(_1Byte), .in2(_2Byte), .out(ByteRead), .sel(selectedblock));  // open: in3
  Multiplexer #(.select(2), .width(32), .enable("false")) multiplexer_4 (
    .in0(_0Line), .in1(_1Line), .in2(_2Line), .in3({32{1'b0}}), .out(Line2Mem), .sel(selectedblock));

  // Other names for the same wires on the sheet: S0 = State[0]; S1 = State[1]; S2 = State[2]; ThisSet = This_Set

  // Notes on the sheet:
  //   Decoding state
  //   These were butners states from lecture
  //   setEnable will be one only if this set is the one we are supposed to be working with
  //   Save the value of contains for all the next states
  //   Select block to choose or evict
  //   choose block to evict
  //   choose block that contains
  //   Return the selected blocks memory
  //   return the selected blocks readbyte
endmodule

module Block (
  input  [2:0] State,
  input  CPURead,
  input  CPUWrite,
  input  [6:0] Tag,
  input  [1:0] Offset,
  input  [7:0] WriteValue,
  input  [31:0] LineFromMem,
  input  SetEnable,
  input  CLK,
  input  [1:0] BlockNumber,
  output Contains,
  output Valid,
  output Dirty,
  output [1:0] updatedAge,
  output [7:0] ByteRead,
  output [31:0] Line2Mem
);

  wire and_1_out, comparator_1_eq, comparator_2_eq, comparator_3_eq, comparator_4_eq, Contains_t,
       demultiplexer_2_out0, demultiplexer_2_out4, Intialize, MemRead, MemWrite, multiplexer_1_out,
       multiplexer_2_out, multiplexer_3_out, or_1_out, or_2_out, Ready, SetAge, SetByte, SetLine, xor_1_out,
       xor_2_out;
  wire [1:0] IncrementAge_updatedage, multiplexer_8_out;
  wire [6:0] StoredTag;
  wire [7:0] multiplexer_4_out, multiplexer_5_out, multiplexer_6_out, multiplexer_7_out, register_1_q;
  wire [31:0] register_3_q;

  Demultiplexer #(.select(3), .enable("false")) demultiplexer_1 (
    .out0(Intialize), .out1(Ready), .out2(MemWrite), .out3(MemRead), .out4(SetAge), .out5(SetLine),
    .out6(SetByte), .out7(Contains_t), .in(1'b1), .sel(State));
  or or_1 (or_1_out, MemRead, MemWrite);
  Register #(.width(7)) u_State (.D(Tag), .en(or_1_out), .Q(StoredTag), .clk(CLK));  // open: clr
  Multiplexer #(.enable("false")) multiplexer_1 (.in0(1'b1), .in1(1'b0), .out(multiplexer_1_out), .sel(MemRead));
  Multiplexer #(.enable("false")) multiplexer_2 (.in0(1'b0), .in1(1'b1), .out(multiplexer_2_out), .sel(MemRead));
  Multiplexer #(.enable("false")) multiplexer_3 (
    .in0(multiplexer_1_out), .in1(1'b0), .out(multiplexer_3_out), .sel(Intialize));
  Demultiplexer #(.select(3), .enable("false")) demultiplexer_2 (
    .out0(demultiplexer_2_out0), .out4(demultiplexer_2_out4), .in(1'b1), .sel(State));  // open: out1, out2, out3, out5, out6, out7
  xor xor_1 (xor_1_out, MemRead, Intialize);
  ExactlyOne xor_2 (.out(xor_2_out), .in0(MemRead), .in1(MemWrite), .in2(Intialize));
  Multiplexer #(.width(8), .enable("false")) multiplexer_4 (
    .in0(WriteValue), .in1(LineFromMem[7:0]), .out(multiplexer_4_out), .sel(MemRead));
  Multiplexer #(.width(8), .enable("false")) multiplexer_5 (
    .in0(WriteValue), .in1(LineFromMem[15:8]), .out(multiplexer_5_out), .sel(MemRead));
  Multiplexer #(.width(8), .enable("false")) multiplexer_6 (
    .in0(WriteValue), .in1(LineFromMem[23:16]), .out(multiplexer_6_out), .sel(MemRead));
  Multiplexer #(.width(8), .enable("false")) multiplexer_7 (
    .in0(WriteValue), .in1(LineFromMem[31:24]), .out(multiplexer_7_out), .sel(MemRead));
  IncrementAge IncrementAge (.ageOfEvicted(2'b10), .currentAge(updatedAge), .updatedAge(IncrementAge_updatedage));
  Register #(.width(1)) State_2 (.D(multiplexer_2_out), .en(xor_1_out), .Q(Valid), .clk(CLK));  // open: clr
  Register #(.width(1)) State_3 (.D(multiplexer_3_out), .en(xor_2_out), .Q(Dirty), .clk(CLK));  // open: clr
  Comparator #(.width(2), .mode("unsigned")) comparator_1 (
    .a(Offset), .b(2'b00), .eq(comparator_1_eq));  // open: gt, lt
  Comparator #(.width(2), .mode("unsigned")) comparator_2 (
    .a(Offset), .b(2'b01), .eq(comparator_2_eq));  // open: gt, lt
  Register register_1 (.D(multiplexer_6_out), .en(comparator_3_eq), .Q(register_1_q), .clk(CLK));  // open: clr
  Comparator #(.width(2), .mode("unsigned")) comparator_3 (
    .a(Offset), .b(2'b10), .eq(comparator_3_eq));  // open: gt, lt
  Register register_2 (.D(multiplexer_7_out), .en(comparator_4_eq), .Q(register_3_q[31:24]), .clk(CLK));  // open: clr
  Comparator #(.width(2), .mode("unsigned")) comparator_4 (
    .a(Offset), .b(2'b11), .eq(comparator_4_eq));  // open: gt, lt
  Multiplexer #(.select(3), .width(2), .enable("false")) multiplexer_8 (
    .in0(BlockNumber), .in1(IncrementAge_updatedage), .in2(IncrementAge_updatedage),
    .in3(IncrementAge_updatedage), .in4(IncrementAge_updatedage), .in5(IncrementAge_updatedage),
    .in6(IncrementAge_updatedage), .in7(IncrementAge_updatedage), .out(multiplexer_8_out), .sel(State));
  or or_2 (or_2_out, demultiplexer_2_out0, demultiplexer_2_out4);
  Register register_3 (.D(multiplexer_4_out), .en(comparator_1_eq), .Q(register_3_q[7:0]), .clk(CLK));  // open: clr
  Register register_4 (.D(multiplexer_5_out), .en(comparator_2_eq), .Q(register_3_q[15:8]), .clk(CLK));  // open: clr
  and and_1 (and_1_out, or_2_out, SetEnable);
  Register #(.width(2)) register_5 (.D(multiplexer_8_out), .en(and_1_out), .Q(updatedAge), .clk(CLK));  // open: clr
  Comparator #(.width(7), .mode("unsigned")) comparator_5 (.a(Tag), .b(StoredTag), .eq(Contains));  // open: gt, lt
  Multiplexer #(.width(8), .enable("false")) multiplexer_9 (
    .in0({8{1'b0}}), .in1(WriteValue), .out(ByteRead), .sel(Contains));
  Register #(.width(32)) register_6 (
    .D({register_3_q[31:24], register_1_q, register_3_q[15:0]}), .en(MemWrite), .Q(Line2Mem), .clk(CLK));  // open: clr

  // Other names for the same wires on the sheet: contain = Contains; CurrAge[1:0] = updatedAge; StoredDirty = Dirty;
  //   StoredValid = Valid

  // Notes on the sheet:
  //   Decoding state
  //   These were butners states from lecture
  //   block number identifies which block we are in
  //   Always evict age of 2
  //   intializing and modifying valid bit
  //   intializing and modifying dirty bit
  //   Set age to block number if initalizing, and update age otherwise
  //   Only update age in intialization and ageupdate states
  //   if the tag matches the storedtag in the block, it contains
  //   and also only if this is the correct set
  //   if not contains, we dont read anything
endmodule

module FSM (
  input  S0,
  input  S1,
  input  S2,
  input  Contains,
  input  Read,
  input  Write,
  output S02,
  output S12,
  output S22,
  output Ready
);

  wire and_1_out, and_2_out, and_3_out, and_4_out, and_5_out, and_6_out, and_7_out, and_8_out, and_9_out,
       and_10_out, and_11_out, and_12_out, and_13_out, and_14_out, and_15_out, not_1_out, not_2_out,
       not_3_out, not_4_out, not_5_out, not_6_out, not_7_out, not_8_out, not_9_out, not_10_out, not_11_out,
       not_12_out, not_13_out, not_14_out, not_15_out, not_16_out, not_17_out, not_18_out, not_19_out,
       not_20_out, not_21_out, not_22_out, not_23_out, not_24_out;

  not not_1 (not_1_out, S0);
  not not_2 (not_2_out, S0);
  not not_3 (not_3_out, S0);
  not not_4 (not_4_out, S1);
  not not_5 (not_5_out, S1);
  not not_6 (not_6_out, Contains);
  not not_7 (not_7_out, S1);
  not not_8 (not_8_out, Contains);
  not not_9 (not_9_out, S1);
  not not_10 (not_10_out, S0);
  not not_11 (not_11_out, S1);
  not not_12 (not_12_out, Read);
  not not_13 (not_13_out, Write);
  not not_14 (not_14_out, S1);
  not not_15 (not_15_out, S2);
  not not_16 (not_16_out, S0);
  not not_17 (not_17_out, S1);
  not not_18 (not_18_out, S0);
  not not_19 (not_19_out, S1);
  not not_20 (not_20_out, S2);
  not not_21 (not_21_out, S0);
  not not_22 (not_22_out, S1);
  not not_23 (not_23_out, Read);
  not not_24 (not_24_out, Write);
  and and_1 (and_1_out, not_1_out, S2, Contains, Write);
  and and_2 (and_2_out, not_2_out, S2, Contains, Read);
  and and_3 (and_3_out, not_3_out, S1);
  and and_4 (and_4_out, S0, not_4_out);
  and and_5 (and_5_out, not_5_out, S2, not_6_out, Write);
  and and_6 (and_6_out, not_7_out, S2, not_8_out, Read);
  and and_7 (and_7_out, S0, not_9_out, S2);
  and and_8 (and_8_out, not_10_out, not_11_out, not_12_out, not_13_out);
  and and_9 (and_9_out, not_14_out, not_15_out);
  and and_10 (and_10_out, not_16_out, not_17_out, Contains);
  and and_11 (and_11_out, S0, Write);
  and and_12 (and_12_out, S0, S1);
  and and_13 (and_13_out, not_18_out, not_19_out, not_20_out);
  and and_14 (and_14_out, not_21_out, not_22_out, not_23_out, not_24_out);
  and and_15 (and_15_out, S0, S1);
  or or_1 (S02, and_1_out, and_2_out, and_3_out, and_4_out);
  or or_2 (S12, and_5_out, and_6_out, and_7_out);
  or or_3 (S22, and_8_out, and_9_out, and_10_out, and_11_out, and_12_out);
  or or_4 (Ready, and_13_out, and_14_out, and_15_out);
endmodule
